# Fritzing sketch circuito (saved by Fritzing 0.9.3b)
breadboards: 2

parts:
  Raspberry_Pi_1 = Raspberry Pi 3 [part_number=RPI-3-V1.2]
  Part1 = Adafruit ADS1015 12Bit I2C ADC [part_number="Adafruit #1083"]
  Part2 = Adafruit MAX4466 Electret Microphone Amplifier [part_number="Adafruit #1063"]  # not connected
  Part3 = Adafruit TCS34725 RGB Color Sensor [part_number="Adafruit #1334"]
  R1 = Rotary Potentiometer (Small) [maximum_resistance=100kΩ package=THT]
  S1 = Pushbutton [package="[THT]"]
  Part4 = Arduino Uno (Rev3) - ICSP
  U1 = 2-Channel 5v Relay Shield [package=relay-2ch5v10a]
  T2 = TMP36 Temperature Sensor [package="TO92 [THT]"]
  J1 = Infrared Proximity Sensor
  IC1 = L293D [package=THT]
  VCC1 = Battery block 9V
  J2 = Basic Servo
  M1 = DC Motor
  LED1 = RGB LED (com. anode, rbg) [package="5 mm [THT]"]
  R2 = 660 Ω Resistor [package="0603 [SMD]"]
  R3 = 660 Ω Resistor [package="0603 [SMD]"]
  R4 = 660 Ω Resistor [package="0603 [SMD]"]

nets:
  3V3: Raspberry_Pi_1.3v3, Raspberry_Pi_1.3V3, Part1.VDD, Part3.VIN, R1.leg1, Part4.AREF, T2.+Vs, LED1.common_anode
  N1: Raspberry_Pi_1.GPIO2, Part1.SDA, Part3.SDA
  N2: Raspberry_Pi_1.GPIO3, Part1.SCL, Part3.SCL
  GND: Raspberry_Pi_1.GND, Part1.GND, Part3.GND, R1.leg2, S1.Pin_1, S1.Pin_2, Part4.GND, U1.GND, T2.GND, J1.GND, IC1.0V, VCC1.-, J2.gnd
  N3: Raspberry_Pi_1.GPIO17, S1.Pin_3, S1.Pin_4
  N4: Raspberry_Pi_1.GPIO27, R2.Pin_0
  N5: Raspberry_Pi_1.GPIO22, J2.pulse
  N6: Raspberry_Pi_1.GPIO5, U1.IN2
  N7: Raspberry_Pi_1.GPIO6, Part4.A0
  N8: Raspberry_Pi_1.GPIO13, Part4.A1
  N9: Raspberry_Pi_1.GPIO26, J1.Vout
  N10: Raspberry_Pi_1.GPIO16, U1.IN1
  N11: Raspberry_Pi_1.GPIO23, R4.Pin_0
  N12: Raspberry_Pi_1.GPIO18, R3.Pin_0
  VCC: Raspberry_Pi_1.5V, U1.VCC, J1.Vcc, J2.vcc
  N13: Part1.AIN1, R1.wiper
  N14: Part1.AIN0, T2.Vout
  N15: Part4.D9_PWM, IC1.Enable_1
  N16: Part4.D2, IC1.In_2
  N17: Part4.D3_PWM, IC1.In_1
  N18: Part4.5V, IC1.+V
  N19: IC1.Out_1_(_Controlled_by_Enable_1_), M1.pin_1
  N20: IC1.Out_2_(_Controlled_by_Enable_1_), M1.pin_2
  N21: IC1.+Vmotor, VCC1.+
  N22: LED1.red_cathode, R2.Pin_1
  N23: LED1.blue_cathode, R3.Pin_1
  N24: LED1.green_cathode, R4.Pin_1

custom parts:
  Adafruit ADS1015 12Bit I2C ADC: For microcontrollers without an analog-to-digital converter or when you want a higher-precision ADC, the ADS1015 provides 12-bit precision at 3300 samples/second over I2C. The chip can be configured as 4 single-ended input channels, or two differential channels. As a nice bonus, it even includes a programmable gain amplifier, up to x16, to help boost up smaller single/differential signals to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
  Adafruit MAX4466 Electret Microphone Amplifier: Add an ear to your project with this well-designed electret microphone amplifier. This fully assembled and tested board comes with a 20-20KHz electret microphone soldered on. For the amplification, we use the Maxim MAX4466, an op-amp specifically designed for this delicate task! The amplifier has excellent power supply noise rejection, so this amplifier sounds really good and isn't nearly as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
  Adafruit TCS34725 RGB Color Sensor: Your electronics can now see in dazzling color with this lovely color light sensor. We found the best color sensor on the market, the TCS34725, which has RGB and Clear light sensing elements. An IR blocking filter, integrated on-chip and localized to the color sensing photodiodes, minimizes the IR spectral component of the incoming light and allows color measurements to be made accurately. The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
  2-Channel 5v Relay Shield: 2 Channel 5v Relay Shield w. 2x SPD-06VDC-SD-C
  660 Ω Resistor: A generic resistor (0.25W)
